// Logisim project Processor.circ as structural Verilog
module main (
  input  RST,
  input  CLR
);

  wire ADD, CLK, decoder_1_out_2, decoder_1_out_3, decoder_1_out_4, decoder_1_out_5, decoder_1_out_6,
       decoder_1_out_7, decoder_1_out_8, decoder_1_out_9, JMN, JMP, LD, LDA, NOP, or_1_out, register_7_q,
       STR, SUB, XCH;
  wire [0:0] or_2_out;
  wire [3:0] INSTRCT;
  wire [4:0] program_counter_1_out_5, register_12_q;
  wire [4:1] register_10_q;
  wire [6:0] AADR, ADDR, multiplexer_1_out;
  wire [10:0] ram_1_data;
  wire [10:8] register_10_q_2;
  wire [15:0] Breg, LOAD, multiplexer_2_out, \Σ ;
  wire [15:7] Areg;

  Hex_Digit_Display hex_digit_display_1 (.value(Areg[15:12]));  // open: dp
  Hex_Digit_Display hex_digit_display_2 (.value(Areg[11:8]));  // open: dp
  Hex_Digit_Display hex_digit_display_3 (.value(Breg[11:8]));  // open: dp
  Hex_Digit_Display hex_digit_display_4 (.value(Breg[15:12]));  // open: dp
  Clock u_CLK (.out(CLK));
  Hex_Digit_Display hex_digit_display_5 (.value({Areg[7], AADR[6:4]}));  // open: dp
  Hex_Digit_Display hex_digit_display_6 (.value(AADR[3:0]));  // open: dp
  Hex_Digit_Display hex_digit_display_7 (.value(Breg[3:0]));  // open: dp
  Hex_Digit_Display hex_digit_display_8 (.value(Breg[7:4]));  // open: dp
  or or_1 (or_1_out, JMP, JMN);
  Program_Counter program_counter_1 (
    .CLK(CLK), .RST(RST), .out_5(program_counter_1_out_5), .JMP_ADDR(register_12_q), .JMP(or_1_out));
  Decoder decoder_1 (
    .out_2(decoder_1_out_2), .out_3(decoder_1_out_3), .out_5(decoder_1_out_5), .out_6(decoder_1_out_6),
    .in_1(INSTRCT), .out_7(decoder_1_out_7), .out_8(decoder_1_out_8), .out_9(decoder_1_out_9),
    .out_4(decoder_1_out_4));  // open: out_10
  RAM #(.addrWidth(5), .dataWidth(11)) ram_1 (
    .addr(program_counter_1_out_5), .data(ram_1_data), .clr(CLR));  // open: sel, clk, ld
  Register #(.width(1)) register_1 (.D(decoder_1_out_2), .Q(ADD), .clk(CLK), .clr(RST));  // open: en
  Register #(.width(1)) register_2 (.D(decoder_1_out_3), .Q(SUB), .clk(CLK), .clr(RST));  // open: en
  Register #(.width(1)) register_3 (.D(decoder_1_out_4), .Q(LD), .clk(CLK), .clr(RST));  // open: en
  Register #(.width(1)) register_4 (.D(decoder_1_out_5), .Q(XCH), .clk(CLK), .clr(RST));  // open: en
  Register #(.width(1)) register_5 (.D(decoder_1_out_6), .Q(STR), .clk(CLK), .clr(RST));  // open: en
  Register #(.width(1)) register_6 (.D(decoder_1_out_7), .Q(JMP), .clk(CLK), .clr(RST));  // open: en
  Register #(.width(1)) register_7 (.D(decoder_1_out_8), .Q(register_7_q), .clk(CLK), .clr(RST));  // open: en
  Register #(.width(1)) register_8 (.D(decoder_1_out_9), .Q(LDA), .clk(CLK), .clr(RST));  // open: en
  Register #(.width(1)) register_9 (.Q(NOP), .clk(CLK), .clr(RST));  // open: D, en
  Register #(.width(11)) register_10 (
    .D(ram_1_data), .Q({register_10_q_2, register_10_q, INSTRCT}), .clk(CLK), .clr(RST));  // open: en
  Register #(.width(7)) register_11 (.D({register_10_q_2, register_10_q}), .Q(ADDR), .clk(CLK), .clr(RST));  // open: en
  Register #(.width(5)) register_12 (
    .D({register_10_q, INSTRCT[3]}), .Q(register_12_q), .clk(CLK), .clr(RST));  // open: en
  and and_1 (JMN, register_7_q, Areg[15]);
  Multiplexer #(.width(7)) multiplexer_1 (.in0(ADDR), .in1(AADR), .out(multiplexer_1_out), .sel(LDA));  // open: en
  or or_2 (or_2_out[0], SUB, ADD);
  _16_bit_Adder_Subtractor u_16_bit_adder_subtractor_1 (
    .B(Breg), .A({Areg, AADR}), .in_1(SUB), .out_4(\Σ ));  // open: OVERFLOW, out_5
  Multiplexer #(.select(3), .width(16)) multiplexer_2 (
    .in0({Areg, AADR}), .in1(\Σ ), .in2(LOAD), .in3({Areg, AADR}), .in4(Breg), .in5({Areg, AADR}),
    .in6({Areg, AADR}), .in7({Areg, AADR}), .out(multiplexer_2_out), .sel({XCH, LD, or_2_out[0]}));  // open: en
  RAM #(.addrWidth(7), .dataWidth(16), .bus("separate")) ram_2 (
    .addr(multiplexer_1_out), .din({Areg, AADR}), .data(LOAD), .str(STR), .clk(CLK), .ld(LD), .clr(CLR));  // open: sel
  Register #(.width(16)) register_13 (.D(multiplexer_2_out), .en(1'b1), .Q({Areg, AADR}), .clk(CLK), .clr(RST));
  Register #(.width(16)) register_14 (.D({Areg, AADR}), .en(XCH), .Q(Breg), .clk(CLK), .clr(RST));

  // Other names for the same wires on the sheet: Areg[6:0] = AADR; NEG = Areg[15]

  // Notes on the sheet:
  //   Program Counter
  //   JMP ADDRESS
  //   Decoder
  //   Program RAM
  //   Instruction Register
  //   Data Memory
  //   Arithmetic Logic Unit
  //   A & B Registers
  //   462.96
endmodule

module FA0 (
  input  A,
  input  B,
  output out_3,
  output out_4
);

  wire nor_1_out;

  nor nor_1 (nor_1_out, B, A);
  and and_1 (out_4, B, A);
  nor nor_2 (out_3, nor_1_out, out_4);

  // Notes on the sheet:
  //   FA0 Circuit - 14 Transistors
  //   Abhijay Saini
endmodule

module FA1 (
  input  in_1,
  input  in_2,
  output out_3,
  output out_4
);

  wire nand_1_out;

  or or_1 (out_4, in_2, in_1);
  nand nand_1 (nand_1_out, in_2, in_1);
  nand nand_2 (out_3, out_4, nand_1_out);
endmodule

module FAopt1 (
  input  A,
  input  B,
  input  Cin,
  output Sum,
  output Cout
);

  wire and_1_out, nand_1_out, nand_2_out, nor_1_out, not_1_out, not_2_out, or_1_out;

  or or_1 (or_1_out, A, B);
  nand nand_1 (nand_1_out, A, B);
  not not_1 (not_1_out, Cin);
  nand nand_2 (nand_2_out, or_1_out, nand_1_out);
  and and_1 (and_1_out, nand_2_out, not_1_out);
  nor nor_1 (nor_1_out, nand_2_out, not_1_out);
  not not_2 (not_2_out, nor_1_out);
  nor nor_2 (Sum, and_1_out, nor_1_out);
  nand nand_3 (Cout, not_2_out, nand_1_out);

  // Notes on the sheet:
  //   FAopt1
  //   Abhijay Saini
  //   36 Transistors
  //   if Cin<2.75, 5.5
  //   if Cin>2.75, Cin+2.75
  //   if Cin<2.75, 4.75
  //   if Cin>2.75, Cin+2
endmodule

module FAopt2 (
  input  A,
  input  B,
  input  Cin,
  output Sum,
  output Cout
);

  wire and_1_out, nand_1_out, nand_2_out, nand_3_out, nand_4_out, nor_1_out, not_1_out, or_1_out;

  or or_1 (or_1_out, A, B);
  nand nand_1 (nand_1_out, A, B);
  not not_1 (not_1_out, Cin);
  nand nand_2 (nand_2_out, or_1_out, nand_1_out);
  and and_1 (and_1_out, nand_2_out, not_1_out);
  nor nor_1 (nor_1_out, nand_2_out, not_1_out);
  nand nand_3 (nand_3_out, B, Cin);
  nand nand_4 (nand_4_out, Cin, A);
  nor nor_2 (Sum, and_1_out, nor_1_out);
  nand nand_5 (Cout, nand_1_out, nand_3_out, nand_4_out);

  // Notes on the sheet:
  //   FAopt2
  //   Abhijay Saini
  //   42 Transistors
  //   if Cin<2.75, 5.5
  //   if Cin>2.75 Cin+2.75
  //   Cin + 2.25
endmodule

module _4_bit (
  input  [3:0] in1,
  input  [3:0] in2,
  output out_3,
  output [3:0] out_4
);

  wire fa0_1_out_4, faopt1_1_cout, faopt2_1_cout;

  FA0 fa0_1 (.out_4(fa0_1_out_4), .B(in1[0]), .out_3(out_4[0]), .A(in2[0]));
  FAopt2 faopt2_1 (.A(in1[1]), .B(in2[1]), .Cin(fa0_1_out_4), .Sum(out_4[1]), .Cout(faopt2_1_cout));
  FAopt1 faopt1_1 (.A(in1[2]), .B(in2[2]), .Cin(faopt2_1_cout), .Sum(out_4[2]), .Cout(faopt1_1_cout));
  FAopt1 faopt1_2 (.A(in1[3]), .B(in2[3]), .Cin(faopt1_1_cout), .Sum(out_4[3]), .Cout(out_3));

  // Notes on the sheet:
  //   Abhijay Saini
  //   120 Transistors
  //   2.75
  //   4-Bit Ripple Carry Adder
  //   4.0
  //   1.75
  //   5.5
  //   6.0
  //   8.75
  //   6.75
  //   8.0
endmodule

module _8_bit (
  input  [7:0] in_1,
  input  [7:0] in_2,
  output out_3,
  output [7:0] out_4
);

  wire fa0_1_out_4, faopt1_1_cout, faopt1_2_cout, faopt1_3_cout, faopt1_4_cout, faopt1_5_cout, faopt2_1_cout;

  FA0 fa0_1 (.out_4(fa0_1_out_4), .B(in_1[0]), .out_3(out_4[0]), .A(in_2[0]));
  FAopt2 faopt2_1 (.A(in_1[1]), .B(in_2[1]), .Cin(fa0_1_out_4), .Sum(out_4[1]), .Cout(faopt2_1_cout));
  FAopt1 faopt1_1 (.A(in_1[2]), .B(in_2[2]), .Cin(faopt2_1_cout), .Sum(out_4[2]), .Cout(faopt1_1_cout));
  FAopt1 faopt1_2 (.A(in_1[3]), .B(in_2[3]), .Cin(faopt1_1_cout), .Sum(out_4[3]), .Cout(faopt1_2_cout));
  FAopt1 faopt1_3 (.A(in_2[5]), .B(in_1[5]), .Cin(faopt1_4_cout), .Sum(out_4[5]), .Cout(faopt1_3_cout));
  FAopt1 faopt1_4 (.A(in_2[4]), .B(in_1[4]), .Cin(faopt1_2_cout), .Sum(out_4[4]), .Cout(faopt1_4_cout));
  FAopt1 faopt1_5 (.A(in_2[6]), .B(in_1[6]), .Cin(faopt1_3_cout), .Sum(out_4[6]), .Cout(faopt1_5_cout));
  FAopt1 faopt1_6 (.A(in_2[7]), .B(in_1[7]), .Cin(faopt1_5_cout), .Sum(out_4[7]), .Cout(out_3));

  // Notes on the sheet:
  //   in1
  //   in2
  //   2.75
  //   1.75
  //   5.5
  //   Abhijay Saini
  //   248 Transistors
  //   4.0
  //   6.75
  //   8-Bit Ripple Carry Adder
  //   6.0
  //   8.75
  //   8.0
  //   10.75
  //   10
  //   12.75
  //   12
  //   14
  //   14.75
  //   16
  //   16.75
endmodule

module _2_1_MUX (
  input  i1,
  input  i0,
  input  Sel,
  output Out
);

  wire nand_1_out, nand_2_out, not_1_out;

  not not_1 (not_1_out, Sel);
  nand nand_1 (nand_1_out, i1, Sel);
  nand nand_2 (nand_2_out, i0, not_1_out);
  nand nand_3 (Out, nand_1_out, nand_2_out);

  // Notes on the sheet:
  //   Abhijay Saini
  //   2:1 MUX
  //   14 Transistors
  //   Timing from Data Inputs = 2.0
  //   Timing from Select = 2.75
endmodule

module _4_1_MUX (
  input  i3,
  input  i2,
  input  i1,
  input  i0,
  input  S0,
  input  S1,
  output Out
);

  wire n2_1_mux_1_out, n2_1_mux_3_out;

  _2_1_MUX u_2_1_mux_1 (.i1(i3), .i0(i2), .Out(n2_1_mux_1_out), .Sel(S1));
  _2_1_MUX u_2_1_mux_2 (.i1(n2_1_mux_1_out), .i0(n2_1_mux_3_out), .Out(Out), .Sel(S0));
  _2_1_MUX u_2_1_mux_3 (.i1(i1), .i0(i0), .Out(n2_1_mux_3_out), .Sel(S1));

  // Notes on the sheet:
  //   Abhijay Saini
  //   4:1 MUX
  //   42 Transistors
  //   Timing from Data Inputs = 4.0
  //   Timing from Select = 5.5
endmodule

module _2_1_MUX_Transmission (
  input  in1,
  input  in0,
  input  Sel,
  output out_4
);

  wire transmission_1_p3, transmission_1_p4;

  // Transmission_Gate #(.gate("br")) transmission_1: pin names not known; wires that end beside it: in1, Sel, transmission_1_p3, transmission_1_p4
  not not_1 (transmission_1_p3, Sel);
  // Transmission_Gate #(.gate("br")) transmission_2: pin names not known; wires that end beside it: in0, transmission_1_p3, Sel, transmission_1_p4
  not not_2 (out_4, transmission_1_p4);

  // Notes on the sheet:
  //   Abhijay Saini
  //   2:1 MUX #2
  //   6 Transistors
  //   Timing from Data Inputs = 1.0
  //   Timing from Select = 1.75
endmodule

module _4_1_MUX_Transmission (
  input  in3,
  input  in2,
  input  in1,
  input  in0,
  input  Sel0,
  input  Sel1,
  output out_7
);

  wire n2_1_mux_transmission_1_out_4, n2_1_mux_transmission_3_out_4;

  _2_1_MUX_Transmission u_2_1_mux_transmission_1 (
    .in1(in3), .in0(in2), .out_4(n2_1_mux_transmission_1_out_4), .Sel(Sel1));
  _2_1_MUX_Transmission u_2_1_mux_transmission_2 (
    .in1(n2_1_mux_transmission_1_out_4), .in0(n2_1_mux_transmission_3_out_4), .out_4(out_7), .Sel(Sel0));
  _2_1_MUX_Transmission u_2_1_mux_transmission_3 (
    .in1(in1), .in0(in0), .out_4(n2_1_mux_transmission_3_out_4), .Sel(Sel1));

  // Notes on the sheet:
  //   Timing from Data Inputs = 2.0
  //   Timing from Select = 3.5
  //   Abhijay Saini
  //   4:1 MUX #2
  //   18 Transistors
endmodule

module _8_bit_CSA (
  input  [7:0] in1,
  input  [7:0] in2,
  output _10_5,
  output [7:0] out_4
);

  wire n2_1_mux_transmission_1_out_4, n2_1_mux_transmission_2_out_4, n2_1_mux_transmission_3_out_4,
       n2_1_mux_transmission_4_out_4, n2_1_mux_transmission_5_out_4, n4_bit_1_out_3, n4_bit_2_out_3,
       n4_bit_adder1_1_out_3;
  wire [3:0] n4_bit_2_out_4, n4_bit_adder1_1_out_4;

  _4_bit u_4_bit_1 (.in1(in2[3:0]), .in2(in1[3:0]), .out_3(n4_bit_1_out_3), .out_4(out_4[3:0]));
  _4_bit u_4_bit_2 (.in1(in2[7:4]), .in2(in1[7:4]), .out_3(n4_bit_2_out_3), .out_4(n4_bit_2_out_4));
  _4_bit_adder1 u_4_bit_adder1_1 (
    .in_1(in2[7:4]), .in_2(in1[7:4]), .out_3(n4_bit_adder1_1_out_3), .out_4(n4_bit_adder1_1_out_4));
  _2_1_MUX_Transmission u_2_1_mux_transmission_1 (
    .in1(n4_bit_adder1_1_out_4[3]), .in0(n4_bit_2_out_4[3]), .out_4(n2_1_mux_transmission_1_out_4),
    .Sel(n4_bit_1_out_3));
  not not_1 (out_4[7], n2_1_mux_transmission_1_out_4);
  _2_1_MUX_Transmission u_2_1_mux_transmission_2 (
    .in1(n4_bit_adder1_1_out_4[2]), .in0(n4_bit_2_out_4[2]), .out_4(n2_1_mux_transmission_2_out_4),
    .Sel(n4_bit_1_out_3));
  not not_2 (out_4[6], n2_1_mux_transmission_2_out_4);
  not not_3 (out_4[5], n2_1_mux_transmission_3_out_4);
  _2_1_MUX_Transmission u_2_1_mux_transmission_3 (
    .in1(n4_bit_adder1_1_out_4[1]), .in0(n4_bit_2_out_4[1]), .out_4(n2_1_mux_transmission_3_out_4),
    .Sel(n4_bit_1_out_3));
  not not_4 (out_4[4], n2_1_mux_transmission_4_out_4);
  _2_1_MUX_Transmission u_2_1_mux_transmission_4 (
    .in1(n4_bit_adder1_1_out_4[0]), .in0(n4_bit_2_out_4[0]), .out_4(n2_1_mux_transmission_4_out_4),
    .Sel(n4_bit_1_out_3));
  not not_5 (_10_5, n2_1_mux_transmission_5_out_4);
  _2_1_MUX_Transmission u_2_1_mux_transmission_5 (
    .in1(n4_bit_adder1_1_out_3), .in0(n4_bit_2_out_3), .out_4(n2_1_mux_transmission_5_out_4),
    .Sel(n4_bit_1_out_3));

  // Notes on the sheet:
  //   8.75
  //   8.0
  //   8.0
  //   Abhijay Saini
  //   400 Transistors
  //   8.0
  //   7
  //   6
  //   5
  //   4
  //   8-bit Carry Select
  //   10.5
endmodule

module _4_bit_adder1 (
  input  [3:0] in_1,
  input  [3:0] in_2,
  output out_3,
  output [3:0] out_4
);

  wire fa1_1_out_4, faopt1_1_cout, faopt2_1_cout;

  FA1 fa1_1 (.out_3(out_4[0]), .out_4(fa1_1_out_4), .in_1(in_1[0]), .in_2(in_2[0]));
  FAopt2 faopt2_1 (.A(in_1[1]), .B(in_2[1]), .Cin(fa1_1_out_4), .Sum(out_4[1]), .Cout(faopt2_1_cout));
  FAopt1 faopt1_1 (.A(in_1[2]), .B(in_2[2]), .Cin(faopt2_1_cout), .Sum(out_4[2]), .Cout(faopt1_1_cout));
  FAopt1 faopt1_2 (.A(in_1[3]), .B(in_2[3]), .Cin(faopt1_1_cout), .Sum(out_4[3]), .Cout(out_3));
endmodule

module _16_bit_CSA (
  input  [15:0] in1,
  input  [15:0] in2,
  output _13,
  output [15:0] out_4
);

  wire n2_1_mux_transmission_1_out_4, n2_1_mux_transmission_2_out_4, n2_1_mux_transmission_3_out_4,
       n2_1_mux_transmission_4_out_4, n2_1_mux_transmission_5_out_4, n2_1_mux_transmission_6_out_4,
       n2_1_mux_transmission_7_out_4, n2_1_mux_transmission_8_out_4, n2_1_mux_transmission_9_out_4,
       n8_bit_csa_1__10_5, n8_bit_csa_2__10_5, n8_bit_csa_adder1_1_out_3;
  wire [7:0] n8_bit_csa_2_out_4, n8_bit_csa_adder1_1_out_4;

  _8_bit_CSA u_8_bit_csa_1 (.in1(in2[7:0]), .in2(in1[7:0]), ._10_5(n8_bit_csa_1__10_5), .out_4(out_4[7:0]));
  _8_bit_CSA u_8_bit_csa_2 (.in1(in2[15:8]), .in2(in1[15:8]), ._10_5(n8_bit_csa_2__10_5), .out_4(n8_bit_csa_2_out_4));
  _8_bit_CSA_adder1 u_8_bit_csa_adder1_1 (
    .in_1(in2[15:8]), .in_2(in1[15:8]), .out_3(n8_bit_csa_adder1_1_out_3), .out_4(n8_bit_csa_adder1_1_out_4));
  _2_1_MUX_Transmission u_2_1_mux_transmission_1 (
    .in1(n8_bit_csa_adder1_1_out_4[7]), .in0(n8_bit_csa_2_out_4[7]), .out_4(n2_1_mux_transmission_1_out_4),
    .Sel(n8_bit_csa_1__10_5));
  _2_1_MUX_Transmission u_2_1_mux_transmission_2 (
    .in1(n8_bit_csa_adder1_1_out_4[6]), .in0(n8_bit_csa_2_out_4[6]), .out_4(n2_1_mux_transmission_2_out_4),
    .Sel(n8_bit_csa_1__10_5));
  _2_1_MUX_Transmission u_2_1_mux_transmission_3 (
    .in1(n8_bit_csa_adder1_1_out_4[5]), .in0(n8_bit_csa_2_out_4[5]), .out_4(n2_1_mux_transmission_3_out_4),
    .Sel(n8_bit_csa_1__10_5));
  _2_1_MUX_Transmission u_2_1_mux_transmission_4 (
    .in1(n8_bit_csa_adder1_1_out_4[4]), .in0(n8_bit_csa_2_out_4[4]), .out_4(n2_1_mux_transmission_4_out_4),
    .Sel(n8_bit_csa_1__10_5));
  _2_1_MUX_Transmission u_2_1_mux_transmission_5 (
    .in1(n8_bit_csa_adder1_1_out_4[3]), .in0(n8_bit_csa_2_out_4[3]), .out_4(n2_1_mux_transmission_5_out_4),
    .Sel(n8_bit_csa_1__10_5));
  _2_1_MUX_Transmission u_2_1_mux_transmission_6 (
    .in1(n8_bit_csa_adder1_1_out_4[2]), .in0(n8_bit_csa_2_out_4[2]), .out_4(n2_1_mux_transmission_6_out_4),
    .Sel(n8_bit_csa_1__10_5));
  _2_1_MUX_Transmission u_2_1_mux_transmission_7 (
    .in1(n8_bit_csa_adder1_1_out_4[1]), .in0(n8_bit_csa_2_out_4[1]), .out_4(n2_1_mux_transmission_7_out_4),
    .Sel(n8_bit_csa_1__10_5));
  _2_1_MUX_Transmission u_2_1_mux_transmission_8 (
    .in1(n8_bit_csa_adder1_1_out_4[0]), .in0(n8_bit_csa_2_out_4[0]), .out_4(n2_1_mux_transmission_8_out_4),
    .Sel(n8_bit_csa_1__10_5));
  not not_1 (out_4[15], n2_1_mux_transmission_1_out_4);
  not not_2 (out_4[14], n2_1_mux_transmission_2_out_4);
  not not_3 (out_4[13], n2_1_mux_transmission_3_out_4);
  not not_4 (out_4[12], n2_1_mux_transmission_4_out_4);
  not not_5 (out_4[11], n2_1_mux_transmission_5_out_4);
  not not_6 (out_4[10], n2_1_mux_transmission_6_out_4);
  not not_7 (out_4[9], n2_1_mux_transmission_7_out_4);
  not not_8 (out_4[8], n2_1_mux_transmission_8_out_4);
  _2_1_MUX_Transmission u_2_1_mux_transmission_9 (
    .in1(n8_bit_csa_adder1_1_out_3), .in0(n8_bit_csa_2__10_5), .out_4(n2_1_mux_transmission_9_out_4),
    .Sel(n8_bit_csa_1__10_5));
  not not_9 (_13, n2_1_mux_transmission_9_out_4);

  // Notes on the sheet:
  //   Abhijay Saini
  //   16-bit Carry Select
  //   1272 Transistors
  //   10.5
  //   10.5
  //   13
endmodule

module _8_bit_CSA_adder1 (
  input  [7:0] in_1,
  input  [7:0] in_2,
  output out_3,
  output [7:0] out_4
);

  wire n2_1_mux_transmission_1_out_4, n2_1_mux_transmission_2_out_4, n2_1_mux_transmission_3_out_4,
       n2_1_mux_transmission_4_out_4, n2_1_mux_transmission_5_out_4, n4_bit_1_out_3, n4_bit_adder1_1_out_3,
       n4_bit_adder1_2_out_3;
  wire [3:0] n4_bit_1_out_4, n4_bit_adder1_2_out_4;

  _4_bit_adder1 u_4_bit_adder1_1 (
    .in_1(in_2[3:0]), .in_2(in_1[3:0]), .out_3(n4_bit_adder1_1_out_3), .out_4(out_4[3:0]));
  _4_bit u_4_bit_1 (.in1(in_2[7:4]), .in2(in_1[7:4]), .out_3(n4_bit_1_out_3), .out_4(n4_bit_1_out_4));
  _4_bit_adder1 u_4_bit_adder1_2 (
    .in_1(in_2[7:4]), .in_2(in_1[7:4]), .out_3(n4_bit_adder1_2_out_3), .out_4(n4_bit_adder1_2_out_4));
  _2_1_MUX_Transmission u_2_1_mux_transmission_1 (
    .in1(n4_bit_adder1_2_out_4[3]), .in0(n4_bit_1_out_4[3]), .out_4(n2_1_mux_transmission_1_out_4),
    .Sel(n4_bit_adder1_1_out_3));
  _2_1_MUX_Transmission u_2_1_mux_transmission_2 (
    .in1(n4_bit_adder1_2_out_4[2]), .in0(n4_bit_1_out_4[2]), .out_4(n2_1_mux_transmission_2_out_4),
    .Sel(n4_bit_adder1_1_out_3));
  _2_1_MUX_Transmission u_2_1_mux_transmission_3 (
    .in1(n4_bit_adder1_2_out_4[1]), .in0(n4_bit_1_out_4[1]), .out_4(n2_1_mux_transmission_3_out_4),
    .Sel(n4_bit_adder1_1_out_3));
  _2_1_MUX_Transmission u_2_1_mux_transmission_4 (
    .in1(n4_bit_adder1_2_out_4[0]), .in0(n4_bit_1_out_4[0]), .out_4(n2_1_mux_transmission_4_out_4),
    .Sel(n4_bit_adder1_1_out_3));
  not not_1 (out_4[7], n2_1_mux_transmission_1_out_4);
  not not_2 (out_4[6], n2_1_mux_transmission_2_out_4);
  not not_3 (out_4[5], n2_1_mux_transmission_3_out_4);
  not not_4 (out_4[4], n2_1_mux_transmission_4_out_4);
  _2_1_MUX_Transmission u_2_1_mux_transmission_5 (
    .in1(n4_bit_adder1_2_out_3), .in0(n4_bit_1_out_3), .out_4(n2_1_mux_transmission_5_out_4),
    .Sel(n4_bit_adder1_1_out_3));
  not not_5 (out_3, n2_1_mux_transmission_5_out_4);

  // Notes on the sheet:
  //   7
  //   6
  //   5
  //   4
endmodule

module _16_bit_Adder_Subtractor (
  input  in_1,
  input  [15:0] B,
  input  [15:0] A,
  output [15:0] out_4,
  output out_5,
  output OVERFLOW
);

  wire nand_1_out, nand_2_out, not_2_out, not_3_out, not_4_out;
  wire [15:0] multiplexer_1_out, not_1_out;

  assign not_1_out = ~B;  // NOT_Gate not_1, 16 bits wide
  Multiplexer #(.width(16)) multiplexer_1 (.in0(B), .in1(not_1_out), .out(multiplexer_1_out), .sel(in_1));  // open: en
  Adder #(.width(16)) adder_1 (.a(multiplexer_1_out), .b(A), .out(out_4), .cin(in_1), .cout(out_5));
  not not_2 (not_2_out, out_4[15]);
  not not_3 (not_3_out, multiplexer_1_out[15]);
  not not_4 (not_4_out, A[15]);
  nand nand_1 (nand_1_out, A[15], multiplexer_1_out[15], not_2_out);
  nand nand_2 (nand_2_out, not_3_out, not_4_out, out_4[15]);
  nand nand_3 (OVERFLOW, nand_1_out, nand_2_out);
endmodule

module _2_1_MUX_Transmission_16_bit (
  input  [15:0] in_1,
  input  [15:0] in_2
);

  _2_1_MUX_Transmission u_2_1_mux_transmission_1 (.in0(in_1[0]));  // open: in1, out_4, Sel
  _2_1_MUX_Transmission u_2_1_mux_transmission_2 (.in0(in_1[1]));  // open: in1, out_4, Sel
  _2_1_MUX_Transmission u_2_1_mux_transmission_3 (.in0(in_1[2]));  // open: in1, out_4, Sel
  _2_1_MUX_Transmission u_2_1_mux_transmission_4 (.in0(in_1[3]));  // open: in1, out_4, Sel
  _2_1_MUX_Transmission u_2_1_mux_transmission_5 (.in0(in_1[4]));  // open: in1, out_4, Sel
  _2_1_MUX_Transmission u_2_1_mux_transmission_6 (.in0(in_1[5]));  // open: in1, out_4, Sel
  _2_1_MUX_Transmission u_2_1_mux_transmission_7 (.in0(in_1[6]));  // open: in1, out_4, Sel
  _2_1_MUX_Transmission u_2_1_mux_transmission_8 (.in0(in_1[7]));  // open: in1, out_4, Sel
  _2_1_MUX_Transmission u_2_1_mux_transmission_9 (.in0(in_1[8]));  // open: in1, out_4, Sel
  _2_1_MUX_Transmission u_2_1_mux_transmission_10 (.in0(in_1[9]));  // open: in1, out_4, Sel
  _2_1_MUX_Transmission u_2_1_mux_transmission_11 (.in0(in_1[10]));  // open: in1, out_4, Sel
  _2_1_MUX_Transmission u_2_1_mux_transmission_12 ();  // open: in1, in0, out_4, Sel
  _2_1_MUX_Transmission u_2_1_mux_transmission_13 ();  // open: in1, in0, out_4, Sel
  _2_1_MUX_Transmission u_2_1_mux_transmission_14 ();  // open: in1, in0, out_4, Sel
  _2_1_MUX_Transmission u_2_1_mux_transmission_15 ();  // open: in1, in0, out_4, Sel
  _2_1_MUX_Transmission u_2_1_mux_transmission_16 ();  // open: in1, in0, out_4, Sel
endmodule

module CLA__1 (
  input  G3,
  input  G2,
  input  G1,
  input  G0,
  input  P3,
  input  P2,
  input  P1,
  input  P0,
  input  Cin0,
  output out_10
);

  wire and_1_out, and_2_out, and_3_out, and_4_out;

  and and_1 (and_1_out, Cin0, P0, P1, P2, P3);
  and and_2 (and_2_out, P3, P2, P1, G0);
  and and_3 (and_3_out, G1, P3, P2);
  and and_4 (and_4_out, G2, P3);
  or or_1 (out_10, G3, and_1_out, and_2_out, and_3_out, and_4_out);

  // Notes on the sheet:
  //   Abhijay Saini
  //   48 Transistors
  //   Carry Look Ahead Cout3 #1
endmodule

module temp (
  input  B3,
  input  OP,
  input  A3,
  input  R3,
  output OVERFLOW
);

  wire and_1_out, nand_1_out, nand_2_out, nor_1_out, nor_2_out, not_1_out, not_2_out, not_3_out;

  nor nor_1 (nor_1_out, B3, OP);
  and and_1 (and_1_out, OP, B3);
  nor nor_2 (nor_2_out, nor_1_out, and_1_out);
  not not_1 (not_1_out, R3);
  not not_2 (not_2_out, nor_2_out);
  not not_3 (not_3_out, A3);
  nand nand_1 (nand_1_out, A3, nor_2_out, not_1_out);
  nand nand_2 (nand_2_out, not_2_out, not_3_out, R3);
  nand nand_3 (OVERFLOW, nand_1_out, nand_2_out);
endmodule

module Program_Counter (
  input  [4:0] JMP_ADDR,
  input  JMP,
  input  RST,
  input  CLK,
  output [4:0] out_5
);

  wire [4:0] adder_1_out, multiplexer_1_out;

  Adder #(.width(5)) adder_1 (.a(out_5), .b(5'b00001), .out(adder_1_out), .cin(1'b0));  // open: cout
  Multiplexer #(.width(5)) multiplexer_1 (
    .in0(adder_1_out), .in1(JMP_ADDR), .out(multiplexer_1_out), .sel(JMP));  // open: en
  Register #(.width(5)) register_1 (.D(multiplexer_1_out), .Q(out_5), .clk(CLK), .clr(RST));  // open: en
endmodule

module Decoder (
  input  [3:0] in_1,
  output out_2,
  output out_3,
  output out_4,
  output out_5,
  output out_6,
  output out_7,
  output out_8,
  output out_9,
  output out_10
);

  wire and_3_out, not_1_out, not_2_out, not_3_out, not_4_out, not_5_out, not_6_out, not_7_out, not_8_out,
       not_9_out, not_10_out, not_11_out, not_12_out, not_13_out, not_14_out, not_15_out, not_16_out;

  not not_1 (not_1_out, in_1[0]);
  not not_2 (not_2_out, in_1[1]);
  and and_1 (out_2, not_1_out, not_2_out, not_3_out, not_4_out);
  not not_3 (not_3_out, in_1[2]);
  not not_4 (not_4_out, in_1[3]);
  not not_5 (not_5_out, in_1[1]);
  and and_2 (out_3, in_1[0], not_5_out, not_6_out);
  not not_6 (not_6_out, in_1[2]);
  not not_7 (not_7_out, in_1[0]);
  and and_3 (and_3_out, not_7_out, in_1[1], not_8_out);
  not not_8 (not_8_out, in_1[2]);
  and and_4 (out_5, in_1[0], in_1[1], not_9_out);
  not not_9 (not_9_out, in_1[2]);
  not not_10 (not_10_out, in_1[0]);
  not not_11 (not_11_out, in_1[1]);
  and and_5 (out_6, not_10_out, not_11_out, in_1[2]);
  and and_6 (out_7, in_1[0], not_12_out, in_1[2]);
  not not_12 (not_12_out, in_1[1]);
  not not_13 (not_13_out, in_1[0]);
  and and_7 (out_8, not_13_out, in_1[1], in_1[2]);
  and and_8 (out_9, in_1[0], in_1[1], in_1[2]);
  not not_14 (not_14_out, in_1[0]);
  not not_15 (not_15_out, in_1[1]);
  and and_9 (out_10, not_14_out, not_15_out, not_16_out, in_1[3]);
  not not_16 (not_16_out, in_1[2]);
  or or_1 (out_4, and_3_out, out_9);
endmodule
